# Fritzing sketch Machine Error (saved by Fritzing 0.9.3b)
breadboards: 1

parts:
  Part1 = Arduino Uno (Rev3)
  U1 = LCD-16X2 [package=lcd-16x2_noholes]
  LED1 = smd LED [color="Red (633nm)" package="1206 [SMD]"]
  LED2 = smd LED [color="Yellow (595nm)" package="1206 [SMD]"]
  LED3 = smd LED [color="Green (570nm)" package="1206 [SMD]"]
  S1 = Round Pushbutton
  S2 = Round Pushbutton
  S3 = Round Pushbutton
  GSM_SIM_GPSR_SMS_SIM900_SIM1 = SIM800L [package=THT]  # not connected

nets:
  N1: Part1.A0, U1.DB4
  N2: Part1.A1, U1.DB5
  N3: Part1.A2, U1.DB6
  N4: Part1.A3, U1.DB7
  N5: Part1.D8, S1.leg0
  N6: Part1.D9_PWM, S2.leg0
  N7: Part1.D10_PWM/SS, S3.leg0
  N8: Part1.D11_PWM/MOSI, U1.E
  N9: Part1.D12/MISO, U1.RS
  N10: Part1.D6_PWM, U1.VO
  N11: Part1.GND, LED1.anode, LED2.anode, LED3.anode, S1.leg1, S2.leg1, S3.leg1
